// Logisim project Lab2.circ as structural Verilog: 1 circuit, main circuit main
module main (
  input  X,
  input  Y,
  input  Z,
  output out_4
);

  wire nor_1_out, nor_2_out, nor_3_out, not_1_out, not_2_out;

  not not_1 (not_1_out, X);
  not not_2 (not_2_out, Y);
  nor nor_1 (nor_1_out, X, Z);
  nor nor_2 (nor_2_out, not_1_out, Y);
  nor nor_3 (nor_3_out, not_2_out, Z);
  nor nor_4 (out_4, nor_1_out, nor_2_out, nor_3_out);
endmodule
