// Logisim project Lab4.circ as structural Verilog: 1 circuit, main circuit main
module main (
  input  A,
  input  B,
  input  C,
  input  D,
  output out_5
);

  wire and_1_out, and_2_out, and_3_out, nor_1_out, not_1_out, not_2_out, not_3_out, not_4_out, not_5_out;

  not not_1 (not_1_out, A);
  not not_2 (not_2_out, D);
  not not_3 (not_3_out, B);
  not not_4 (not_4_out, A);
  not not_5 (not_5_out, C);
  nor nor_1 (nor_1_out, A, B, D);
  and and_1 (and_1_out, not_1_out, C, not_2_out);
  and and_2 (and_2_out, A, not_3_out, D);
  and and_3 (and_3_out, not_4_out, B, not_5_out, D);
  or or_1 (out_5, nor_1_out, and_1_out, and_2_out, and_3_out);
endmodule
