// Logisim project Lab5.circ as structural Verilog: 1 circuit, main circuit main
module main (
  input  S,
  input  Clock,
  input  R,
  output Q_prime,
  output Q
);

  wire and_1_out, and_2_out;

  and and_1 (and_1_out, S, Clock);
  and and_2 (and_2_out, Clock, R);
  nor nor_1 (Q_prime, and_1_out, Q);
  nor nor_2 (Q, Q_prime, and_2_out);
endmodule
