// Logisim project Lab7.circ as structural Verilog: 1 circuit, main circuit main
module main (
  output out_1
);

  wire clock_1_out, j_k_ff_1_q, j_k_ff_2_q, j_k_ff_2_qn;

  Clock clock_1 (.out(clock_1_out));
  J_K_Flip_Flop j_k_ff_1 (
    .J(j_k_ff_2_q), .clk(clock_1_out), .K(j_k_ff_1_q), .Q(j_k_ff_1_q));  // open: Qn, preset, en, reset
  J_K_Flip_Flop j_k_ff_2 (
    .J(j_k_ff_2_qn), .clk(clock_1_out), .K(j_k_ff_1_q), .Q(j_k_ff_2_q), .Qn(j_k_ff_2_qn));  // open: preset, en, reset
  not not_1 (out_1, j_k_ff_2_qn);
endmodule
